// Logisim project 4.NAND.circ as structural Verilog: 1 circuit, main circuit main
module main (
  input  A,
  input  B,
  output Output
);

  wire and_1_out;

  and and_1 (and_1_out, A, B);
  not not_1 (Output, and_1_out);
endmodule
