// Logisim project 7.XNOR.circ as structural Verilog: 1 circuit, main circuit main
module main (
  input  A,
  input  B,
  output out_3
);

  wire A_prime_B_out, AB_prime_out, not_1_out, not_2_out, or_1_out;

  not not_1 (not_1_out, B);
  not not_2 (not_2_out, A);
  and AB_prime (AB_prime_out, A, not_1_out);
  and A_prime_B (A_prime_B_out, B, not_2_out);
  not not_3 (out_3, or_1_out);
  or or_1 (or_1_out, AB_prime_out, A_prime_B_out);
endmodule
