// Logisim project 4(a).circ as structural Verilog: 1 circuit, main circuit main
module main (
  input  a,
  input  b,
  input  c,
  input  d,
  output \output 
);

  wire a_b_cd__bc_prime__prime_out, a_prime__b_prime_cd_prime___prime_out, a_prime_out, b_cd__prime_out,
       b_cd_out, b_prime_c__prime_out, b_prime_cd_prime_out, b_prime_out, c_out, c_prime_d_prime__prime_out,
       c_prime_out;

  not c_prime (c_prime_out, c);  // NOR_Gate
  not d_prime (c_prime_out, d);  // NOR_Gate
  nor c_prime_d_prime__prime (c_prime_d_prime__prime_out, c_prime_out, c_prime_out);
  not b_prime (b_prime_out, b);  // NOR_Gate
  not u_c (c_out, c_prime_out);  // NOR_Gate
  nor b_cd__prime (b_cd__prime_out, b, c_prime_d_prime__prime_out);
  nor b_prime_c__prime (b_prime_c__prime_out, b_prime_out, c_out);
  not b_prime_cd_prime (b_prime_cd_prime_out, b_cd__prime_out);  // NOR_Gate
  not a_prime (a_prime_out, a);  // NOR_Gate
  not b_cd (b_cd_out, b_prime_cd_prime_out);  // NOR_Gate
  nor a_prime__b_prime_cd_prime___prime (a_prime__b_prime_cd_prime___prime_out, a_prime_out, b_cd_out);
  nor a_b_cd__bc_prime__prime (a_b_cd__bc_prime__prime_out, a_prime__b_prime_cd_prime___prime_out, b_prime_c__prime_out);
  not a_b_cd__bc_prime (\output , a_b_cd__bc_prime__prime_out);  // NOR_Gate
endmodule
