// Logisim project 4(b).circ as structural Verilog: 1 circuit, main circuit main
module main (
  input  a,
  input  b,
  input  c,
  input  d,
  input  e,
  output \output 
);

  wire a_b_prime___cd_e_prime___prime_out, a_prime_b__prime_out, a_prime_out, c_d__prime_2_out,
       c_d__prime_e__prime_out, c_d__prime_out, c_prime_d_prime__prime_out;

  not a_prime (a_prime_out, a);  // NAND_Gate
  nand c_d__prime (c_d__prime_out, c, d);
  not c_prime_d_prime__prime (c_prime_d_prime__prime_out, c_d__prime_out);  // NAND_Gate
  nand a_prime_b__prime (a_prime_b__prime_out, a_prime_out, b);
  not c_d__prime_2 (c_d__prime_2_out, c_prime_d_prime__prime_out);  // NAND_Gate
  nand c_d__prime_e__prime (c_d__prime_e__prime_out, c_d__prime_2_out, e);
  nand a_b_prime___cd_e_prime___prime (a_b_prime___cd_e_prime___prime_out, a_prime_b__prime_out, c_d__prime_e__prime_out);
  not a_b_prime___cd_e_prime (\output , a_b_prime___cd_e_prime___prime_out);  // NAND_Gate
endmodule
