// Logisim project 1.FULL_SUBTRACTOR.circ as structural Verilog: 4 circuits, main circuit main
module main (
  input  A,
  input  B,
  input  C,
  output Difference,
  output Bout
);

  wire A_prime__B_C_out, B_C_2_out, B_C_out, B_XOR_C_out, not_1_out;

  xor B_XOR_C (B_XOR_C_out, B, C);
  not not_1 (not_1_out, A);
  or B_C (B_C_out, B, C);
  and B_C_2 (B_C_2_out, B, C);
  and A_prime__B_C (A_prime__B_C_out, not_1_out, B_C_out);
  xor XOR (Difference, A, B_XOR_C_out);
  or OR (Bout, A_prime__B_C_out, B_C_2_out);

  // Notes on the sheet:
  //   Full Subtractor
  //   A'.(B+C)+B.C
endmodule

module simulator (
  input  X,
  input  Y,
  input  Bin,
  output Difference,
  output Bout
);

  main main_1 (.A(X), .B(Y), .C(Bin), .Difference(Difference), .Bout(Bout));
endmodule

module half_subtractor (
  input  A,
  input  B,
  output Difference,
  output Borrow
);

  wire not_1_out;

  not not_1 (not_1_out, A);
  xor A_XOR_B (Difference, A, B);
  and A_prime_B (Borrow, not_1_out, B);
endmodule

module full_subtractor_using_half_subtractor (
  input  X,
  input  Y,
  input  Bin,
  output Difference,
  output Bout
);

  wire half_subtractor_1_borrow, half_subtractor_1_difference, half_subtractor_2_borrow;

  half_subtractor half_subtractor_1 (
    .A(X), .B(Y), .Difference(half_subtractor_1_difference), .Borrow(half_subtractor_1_borrow));
  half_subtractor half_subtractor_2 (
    .A(half_subtractor_1_difference), .B(Bin), .Difference(Difference), .Borrow(half_subtractor_2_borrow));
  or or_1 (Bout, half_subtractor_2_borrow, half_subtractor_1_borrow);
endmodule
