// Logisim project 1.HALF_SUBTRACTOR.circ as structural Verilog: 2 circuits, main circuit main
module main (
  input  A,
  input  B,
  output Difference,
  output Borrow
);

  wire not_1_out;

  not not_1 (not_1_out, A);
  xor xor_1 (Difference, A, B);
  and and_1 (Borrow, not_1_out, B);

  // Notes on the sheet:
  //   Half Subtractor
endmodule

module simulator (
  input  A,
  input  B,
  output Difference,
  output Borrow
);

  main main_1 (.A(A), .B(B), .Difference(Borrow), .Borrow(Borrow));

  assign Difference = Borrow;
endmodule
