// Logisim project MULTIPLEXER.circ as structural Verilog: 2 circuits, main circuit main
module main (
  input  S1,
  input  S2,
  input  S3,
  input  A1,
  input  A2,
  input  A3,
  input  A4,
  input  A5,
  input  A6,
  input  A7,
  input  A8,
  output Output
);

  wire and_1_out, and_2_out, and_3_out, and_4_out, and_5_out, and_6_out, and_7_out, and_8_out, not_1_out,
       not_2_out, not_3_out;

  not not_1 (not_1_out, S1);
  not not_2 (not_2_out, S2);
  not not_3 (not_3_out, S3);
  and and_1 (and_1_out, A1, not_1_out, not_2_out, not_3_out);
  and and_2 (and_2_out, A2, S1, not_2_out, not_3_out);
  and and_3 (and_3_out, A3, not_1_out, S2, not_3_out);
  and and_4 (and_4_out, A4, S1, S2, not_3_out);
  and and_5 (and_5_out, A5, not_1_out, not_2_out, S3);
  and and_6 (and_6_out, A6, S1, not_2_out, S3);
  and and_7 (and_7_out, A7, not_1_out, S2, S3);
  and and_8 (and_8_out, A8, S1, S2, S3);
  or or_1 (Output, and_1_out, and_2_out, and_3_out, and_4_out, and_5_out, and_6_out, and_7_out, and_8_out);
endmodule

module simulator (
  input  S1,
  input  S2,
  input  S3,
  input  A1,
  input  A2,
  input  A3,
  input  A4,
  input  A5,
  input  A6,
  input  A7,
  input  A8,
  output Output
);

  main main_1 (
    .A1(A1), .A2(A2), .A3(A3), .A4(A4), .A5(A5), .A6(A6), .A7(A7), .A8(A8), .S1(S1), .S2(S2), .S3(S3),
    .Output(Output));
endmodule
