// Logisim project BCDTOEXCESS3.circ as structural Verilog: 1 circuit, main circuit main
module main (
  input  D,
  input  C,
  input  B,
  input  A,
  output W,
  output X,
  output Y,
  output Z
);

  wire B_prime_C_out, B_prime_D_out, BC_out, BC_prime_D_prime_out, BD_out, not_2_out, not_3_out, not_4_out;

  not not_1 (Z, D);
  not not_2 (not_2_out, C);
  not not_3 (not_3_out, B);
  not not_4 (not_4_out, A);
  and BC (BC_out, B, C);
  and BD (BD_out, B, D);
  and B_prime_C (B_prime_C_out, not_3_out, C);
  and B_prime_D (B_prime_D_out, not_3_out, D);
  and BC_prime_D_prime (BC_prime_D_prime_out, B, not_2_out, Z);
  xnor C_XOR_D (Y, C, D);
  or or_1 (W, A, BC_out, BD_out);
  or or_2 (X, B_prime_C_out, B_prime_D_out, BC_prime_D_prime_out);
endmodule
