// Logisim project BINARYTOGRAY.circ as structural Verilog: 2 circuits, main circuit main
module main (
  input  A,
  input  B,
  input  C,
  input  D,
  output W,
  output X,
  output Y,
  output Z
);

  xor A_prime_B_AB_prime (X, A, B);
  xor B_prime_C_BC_prime (Y, B, C);
  xor C_prime_D_CD_prime (Z, C, D);

  assign W = A;

  // Notes on the sheet:
  //   Binary To Gray Code
endmodule

module simulator (
  input  A,
  input  B,
  input  C,
  input  D,
  output W,
  output X,
  output Y,
  output Z
);

  main main_1 (.A(A), .B(B), .C(C), .D(D), .W(W), .X(X), .Y(Y), .Z(Z));
endmodule
