// Logisim project EXCESS3TOBCD.circ as structural Verilog: 1 circuit, main circuit main
module main (
  input  W,
  input  X,
  input  Y,
  input  Z,
  output A,
  output B,
  output C,
  output D
);

  wire not_1_out, not_2_out, not_3_out, WX_out, WYZ_out, X_prime_Y_prime_out, X_prime_Z_prime_out, XYZ_out;

  not not_1 (not_1_out, W);
  not not_2 (not_2_out, X);
  not not_3 (not_3_out, Y);
  not not_4 (D, Z);
  and WX (WX_out, W, X);
  and WYZ (WYZ_out, W, Y, Z);
  and X_prime_Y_prime (X_prime_Y_prime_out, not_2_out, not_3_out);
  and X_prime_Z_prime (X_prime_Z_prime_out, not_2_out, D);
  and XYZ (XYZ_out, X, Y, Z);
  xor Y_XOR_Z (C, Y, Z);
  or or_1 (A, WX_out, WYZ_out);
  or or_2 (B, X_prime_Y_prime_out, X_prime_Z_prime_out, XYZ_out);
endmodule
