// Logisim project GRAYTOBCD.circ as structural Verilog: 1 circuit, main circuit main
module main (
  input  G3,
  input  G2,
  input  G1,
  input  G0,
  output B3,
  output B2,
  output B1,
  output B0
);

  wire G2_prime_G1_out, G2_prime_G1_prime_G0_prime_out, G2_prime_G1G0_prime_out, G2G1G0_out,
       G3_prime_G2G1_prime_G0_prime_out, G3_prime_G2G1_prime_out, G3G0_out, not_1_out, not_2_out, not_3_out,
       not_4_out;

  not not_1 (not_1_out, G3);
  not not_2 (not_2_out, G2);
  not not_3 (not_3_out, G1);
  not not_4 (not_4_out, G0);
  and G3_prime_G2 (B2, not_1_out, G2);
  and G2_prime_G1 (G2_prime_G1_out, not_2_out, G1);
  and G3_prime_G2G1_prime (G3_prime_G2G1_prime_out, not_1_out, G2, not_3_out);
  and G2_prime_G1G0_prime (G2_prime_G1G0_prime_out, not_2_out, G1, not_4_out);
  and G2G1G0 (G2G1G0_out, G2, G1, G0);
  and G3G0 (G3G0_out, G3, G0);
  and G2_prime_G1_prime_G0_prime (G2_prime_G1_prime_G0_prime_out, not_2_out, not_3_out, G0);
  and G3_prime_G2G1_prime_G0_prime (G3_prime_G2G1_prime_G0_prime_out, not_1_out, G2, not_3_out, not_4_out);
  or or_1 (B1, G2_prime_G1_out, G3_prime_G2G1_prime_out);
  or or_2 (B0, G2_prime_G1G0_prime_out, G2G1G0_out, G3G0_out, G2_prime_G1_prime_G0_prime_out, G3_prime_G2G1_prime_G0_prime_out);

  assign B3 = G3;
endmodule
