// Logisim project GRAYTOBINARY.circ as structural Verilog: 2 circuits, main circuit main
module main (
  input  W,
  input  X,
  input  Y,
  input  Z,
  output A,
  output B,
  output C,
  output D
);

  xor xor_1 (B, W, X);
  xor xor_2 (C, B, Y);
  xor xor_3 (D, C, Z);

  assign A = W;

  // Notes on the sheet:
  //   Gray To Binary Code
endmodule

module simulator (
  input  W,
  input  X,
  input  Y,
  input  Z,
  output A,
  output B,
  output C,
  output D
);

  main main_1 (.W(W), .X(X), .Y(Y), .Z(Z), .A(A), .B(B), .C(C), .D(D));
endmodule
