// Logisim project 1.FULL_ADDER.circ as structural Verilog: 2 circuits, main circuit main
module main (
  input  X,
  input  Y,
  input  Z,
  output SUM,
  output CARRY
);

  wire not_1_out, not_2_out, not_3_out, not_4_out, not_5_out, not_6_out, X_prime_Y_out,
       X_prime_Y_prime_Z_out, X_prime_Y_Y_nX__Z_out, X_prime_Y_Y_prime_X_out, X_prime_Y_Z_prime_out, X_Y_out,
       X_Y_prime_Z_prime_out, X_Y_Z_out, Y_prime_X_out;

  not not_1 (not_1_out, X);
  not not_2 (not_2_out, X);
  not not_3 (not_3_out, X);
  not not_4 (not_4_out, X);
  not not_5 (not_5_out, X);
  not not_6 (not_6_out, X);
  and X_prime_Y_prime_Z (X_prime_Y_prime_Z_out, not_1_out, not_2_out, X);
  and X_prime_Y_Z_prime (X_prime_Y_Z_prime_out, not_3_out, X, not_4_out);
  and X_Y_prime_Z_prime (X_Y_prime_Z_prime_out, X, not_5_out, not_6_out);
  and X_Y_Z (X_Y_Z_out, X, X, X);
  and X_Y (X_Y_out, X, X);
  and X_prime_Y (X_prime_Y_out, not_1_out, X);
  and Y_prime_X (Y_prime_X_out, not_2_out, X);
  or X_prime_Y_Y_prime_X (X_prime_Y_Y_prime_X_out, X_prime_Y_out, Y_prime_X_out);
  or X_prime_Y_prime_Z_X_prime_Y_Z_prime_X_Y_prime_Z_prime_X_Y_Z (SUM, X_prime_Y_prime_Z_out, X_prime_Y_Z_prime_out, X_Y_prime_Z_prime_out, X_Y_Z_out);
  and X_prime_Y_Y_nX__Z (X_prime_Y_Y_nX__Z_out, X_prime_Y_Y_prime_X_out, X);
  or XY__X_prime_Y_Y_prime_X_Z (CARRY, X_Y_out, X_prime_Y_Y_nX__Z_out);

  assign Y = X;
  assign Z = X;

  // Notes on the sheet:
  //   FULL ADDER
endmodule

module simulator (
  input  X,
  input  Y,
  input  Z,
  output S,
  output C
);

  main main_1 (.X(X), .Y(Y), .Z(Z), .SUM(S), .CARRY(C));

  // Notes on the sheet:
  //   FA
  //   SIMULATOR
endmodule
