// Logisim project 1.HALF_ADDER.circ as structural Verilog: 3 circuits, main circuit main
module main (
  input  X,
  input  Y,
  output Sum,
  output Carry
);

  wire not_1_out, not_2_out, X_prime_Y_out, X_Y_prime_out;

  not not_1 (not_1_out, X);
  not not_2 (not_2_out, Y);
  and X_prime_Y (X_prime_Y_out, not_1_out, Y);
  and X_Y_prime (X_Y_prime_out, X, not_2_out);
  and X_Y (Carry, X, Y);
  or X_prime_Y_X_Y_prime (Sum, X_prime_Y_out, X_Y_prime_out);

  // Notes on the sheet:
  //   HALF ADDER
endmodule

module simulator (
  input  X,
  input  Y,
  output S,
  output C
);

  main main_1 (.X(X), .Y(Y), .Sum(S), .Carry(C));

  // Notes on the sheet:
  //   HA
  //   SIMULATOR
endmodule

module _4_bit_magnite_adder (
  input  Cin,
  input  X0,
  input  X1,
  input  X2,
  input  X3,
  output S0,
  output S1,
  output S2,
  output S3,
  output Cout
);

  wire main_1_carry, main_2_carry, main_3_carry;

  main main_1 (.X(Cin), .Y(X0), .Sum(S0), .Carry(main_1_carry));
  main main_2 (.X(main_1_carry), .Y(X1), .Sum(S1), .Carry(main_2_carry));
  main main_3 (.X(main_2_carry), .Y(X2), .Sum(S2), .Carry(main_3_carry));
  main main_4 (.X(main_3_carry), .Y(X3), .Sum(S3), .Carry(Cout));

  // Notes on the sheet:
  //   HA
  //   HA
  //   HA
  //   HA
  //   4 BIT MAGNITE ADDER
endmodule
