// Logisim project 1.AND_USING_NAND.circ as structural Verilog: 1 circuit, main circuit main
module main (
  input  A,
  input  B,
  output Output
);

  wire n_A_B_out;

  nand n_A_B (n_A_B_out, A, B);
  not nn_A_B (Output, n_A_B_out);  // NAND_Gate
endmodule
