// Logisim project 2.OR_USING_NAND.circ as structural Verilog: 1 circuit, main circuit main
module main (
  input  A,
  input  B,
  output Output
);

  wire nA_out, nB_out;

  not nA (nA_out, A);  // NAND_Gate
  not nB (nB_out, B);  // NAND_Gate
  nand n_nA__nB (Output, nA_out, nB_out);
endmodule
