// Logisim project 4.XOR_USING_NAND.circ as structural Verilog: 1 circuit, main circuit main
module main (
  input  A,
  input  B,
  output Output
);

  wire n_A_nB_out, n_nA_B_out, nA_out, nB_out;

  not nA (nA_out, A);  // NAND_Gate
  not nB (nB_out, B);  // NAND_Gate
  nand n_nA_B (n_nA_B_out, nA_out, B);
  nand n_A_nB (n_A_nB_out, A, nB_out);
  nand nand_1 (Output, n_nA_B_out, n_A_nB_out);
endmodule
