// Logisim project 1.AND_USING_NOR.circ as structural Verilog: 1 circuit, main circuit main
module main (
  input  A,
  input  B,
  output Output
);

  wire nA_out, nB_out;

  not nA (nA_out, A);  // NOR_Gate
  not nB (nB_out, B);  // NOR_Gate
  nor n_nA_nB (Output, nA_out, nB_out);
endmodule
