// Logisim project 2.OR_USING_NOR.circ as structural Verilog: 1 circuit, main circuit main
module main (
  input  A,
  input  B,
  output Output
);

  wire n_A_B_out;

  nor n_A_B (n_A_B_out, A, B);
  not nn_A_B (Output, n_A_B_out);  // NOR_Gate
endmodule
