// Logisim project 4.XOR_USING_NOR.circ as structural Verilog: 1 circuit, main circuit main
module main (
  input  A,
  input  B,
  output out_3
);

  wire A_nB_out, nA_B_out, nA_out, nB_out, nor_1_out;

  not nA (nA_out, A);  // NOR_Gate
  not nB (nB_out, B);  // NOR_Gate
  nor nA_B (nA_B_out, nA_out, B);
  nor A_nB (A_nB_out, A, nB_out);
  nor nor_1 (nor_1_out, nA_B_out, A_nB_out);
  not nor_2 (out_3, nor_1_out);  // NOR_Gate
endmodule
