// Logisim project 5.XNOR_USING_NOR.circ as structural Verilog: 1 circuit, main circuit main
module main (
  input  A,
  input  B,
  output out_3
);

  wire n_A_nB_out, n_nA_B_out, nA_out, nB_out, nor_1_out, nor_2_out;

  not nA (nA_out, A);  // NOR_Gate
  not nB (nB_out, B);  // NOR_Gate
  nor n_nA_B (n_nA_B_out, nA_out, B);
  nor n_A_nB (n_A_nB_out, A, nB_out);
  nor nor_1 (nor_1_out, n_nA_B_out, n_A_nB_out);
  not nor_2 (nor_2_out, nor_1_out);  // NOR_Gate
  not nor_3 (out_3, nor_2_out);  // NOR_Gate
endmodule
